// Logisim project CPU.circ as structural Verilog: 9 circuits, main circuit main
module main (
  input  GO
);

  wire clock_1_out, new_decoder_1_halt, newfsm_1_memenable, newfsm_1_memwrite, newfsm_1_pc_increment,
       newfsm_1_regwrite, not_1_out;
  wire [1:0] newfsm_1_pcsource, newfsm_1_wbsource;
  wire [2:0] new_decoder_1_rd, new_decoder_1_rs, new_decoder_1_rt, newfsm_1_aluop, newfsm_1_state_register;
  wire [3:0] alu_1_nzvc, new_decoder_1_opcode;
  wire [5:0] new_decoder_1_load_store_offset;
  wire [7:0] adder_1_out, adder_2_out, alu_1_out_5, bit_extender_1_out, controlled_buffer_1_out,
       multiplexer_1_out, multiplexer_2_out, multiplexer_3_out, new_decoder_1_immediate_address,
       new_decoder_1_immediate_number, PC_q, register_file_1_destination__store_only,
       register_file_1_source_2, register_file_1_target_2;
  wire [15:0] IR_q, rom_1_data;

  Clock clock_1 (.out(clock_1_out));
  Register PC (.D(multiplexer_1_out), .en(newfsm_1_pc_increment), .Q(PC_q), .clk(clock_1_out));  // open: clr
  Adder adder_1 (.a(8'h1), .b(PC_q), .out(adder_1_out));  // open: cin, cout
  Adder adder_2 (.a(adder_1_out), .b(bit_extender_1_out), .out(adder_2_out));  // open: cin, cout
  Multiplexer #(.select(2), .width(8), .disabled(0), .enable("false")) multiplexer_1 (
    .in0(adder_1_out), .in1(adder_2_out), .in2(new_decoder_1_immediate_address),
    .in3(register_file_1_source_2), .out(multiplexer_1_out), .sel(newfsm_1_pcsource));
  ROM #(.dataWidth(16)) rom_1 (.addr(PC_q), .data(rom_1_data));  // open: sel
  Register #(.width(16)) IR (.D(rom_1_data), .Q(IR_q), .clk(clock_1_out));  // open: en, clr
  // Probe on newfsm_1_state_register
  NewFSM newfsm_1 (
    .NZVC(alu_1_nzvc), .State_Register(newfsm_1_state_register), .CLK(clock_1_out), .ALUOp(newfsm_1_aluop),
    .MemWrite(newfsm_1_memwrite), .PCSource(newfsm_1_pcsource), .RegWrite(newfsm_1_regwrite),
    .WBsource(newfsm_1_wbsource), .GO(GO), .PC_increment(newfsm_1_pc_increment),
    .Instruction_OPcode(new_decoder_1_opcode), .Halt(new_decoder_1_halt), .MemEnable(newfsm_1_memenable));
  New_Decoder new_decoder_1 (
    .Instruction(IR_q), .OPCODE(new_decoder_1_opcode), .Immediate_Address(new_decoder_1_immediate_address),
    .Load_Store_offset(new_decoder_1_load_store_offset), .Rt(new_decoder_1_rt), .Rd(new_decoder_1_rd),
    .Rs(new_decoder_1_rs), .Immediate_Number(new_decoder_1_immediate_number), .Halt(new_decoder_1_halt));
  Multiplexer #(.select(2), .width(8), .disabled(0), .enable("false")) multiplexer_2 (
    .in0(new_decoder_1_immediate_number), .in1(adder_1_out), .in2(controlled_buffer_1_out),
    .in3(alu_1_out_5), .out(multiplexer_2_out), .sel(newfsm_1_wbsource));
  assign bit_extender_1_out = {{2{new_decoder_1_load_store_offset[5]}}, new_decoder_1_load_store_offset};  // Bit_Extender bit_extender_1
  assign controlled_buffer_1_out = newfsm_1_memwrite ? register_file_1_destination__store_only : 8'bz;  // Controlled_Buffer controlled_buffer_1
  Register_File register_file_1 (
    .Source(new_decoder_1_rs), .Target(new_decoder_1_rt), .Write_Back__RD(multiplexer_2_out),
    .Clk(clock_1_out), .Destination(new_decoder_1_rd), .Source_2(register_file_1_source_2),
    .Target_2(register_file_1_target_2), .Destination__Store_ONLY(register_file_1_destination__store_only),
    .RegWrite(newfsm_1_regwrite));
  Multiplexer #(.width(8), .disabled(0), .enable("false")) multiplexer_3 (
    .in0(register_file_1_target_2), .in1(bit_extender_1_out), .out(multiplexer_3_out),
    .sel(newfsm_1_memenable));
  ALU alu_1 (
    .A(register_file_1_source_2), .B(multiplexer_3_out), .Op_Code(newfsm_1_aluop), .NZVC(alu_1_nzvc),
    .out_5(alu_1_out_5));
  not not_1 (not_1_out, newfsm_1_memwrite);
  // Probe on controlled_buffer_1_out
  RAM ram_1 (
    .addr(alu_1_out_5), .data(controlled_buffer_1_out), .sel(newfsm_1_memenable), .clk(clock_1_out),
    .ld(not_1_out));  // open: clr

  // Notes on the sheet:
  //   PC+1
  //   Instruction memory
  //   contents of rom_1 (hex, n*v repeats v):
  //   2c0a 2a00 2801 2200 2401 8650 8280 84c0 8b60 1740 6bba f000 4*0 96d0 1600 5000 221*0 8688 5000
  //   Execution Memory
endmodule

module ALU (
  input  [7:0] A,
  input  [7:0] B,
  input  [2:0] Op_Code,
  output [3:0] NZVC,
  output [7:0] out_5
);

  wire bitselector_1_out, bitselector_2_out, comparator_1_gt, nor_1_out;
  wire [7:0] addsub_1_result, and_1_out, bit_extender_1_out, not_1_out, or_1_out, shift_unit_1_shift_result,
       xor_1_out;

  // Probe on A
  // Probe on A
  // Probe on B
  // Probe on B
  BitSelector bitselector_1 (.in(A), .out(bitselector_1_out), .sel(3'b111));
  Comparator comparator_1 (.a(A), .b(B), .gt(comparator_1_gt));  // open: eq, lt
  BitSelector bitselector_2 (.in(B), .out(bitselector_2_out), .sel(3'b111));
  nor nor_1 (nor_1_out, Op_Code[1], Op_Code[2]);
  AddSub addsub_1 (
    .A(A), .B(B), .ADD_0_SUB_1(Op_Code[0]), .Result(addsub_1_result), .Carry(NZVC[0]),
    .Is_Add_or_Sub(nor_1_out));
  assign not_1_out = ~A;  // NOT_Gate not_1, 8 bits wide
  assign or_1_out = A | B;  // OR_Gate or_1, 8 bits wide
  assign and_1_out = A & B;  // AND_Gate and_1, 8 bits wide
  assign xor_1_out = A ^ B;  // XOR_Gate xor_1, 8 bits wide
  Shift_unit shift_unit_1 (.A(A), .B(B), .Shift_result(shift_unit_1_shift_result));
  assign bit_extender_1_out = {{7{1'b0}}, comparator_1_gt};  // Bit_Extender bit_extender_1
  Overflow_detect overflow_detect_1 (
    .MSB_A(bitselector_1_out), .MSB_B(bitselector_2_out), .MSB_Result(NZVC[3]),
    ._0_for_Add_1_for_Sub(Op_Code[0]), .Overflow_FLAG(NZVC[1]), .Is_Add_or_Sub(nor_1_out));
  Multiplexer #(.select(3), .width(8), .disabled(0)) multiplexer_1 (
    .in0(addsub_1_result), .in1(addsub_1_result), .in2(not_1_out), .in3(or_1_out), .in4(and_1_out),
    .in5(xor_1_out), .in6(shift_unit_1_shift_result), .in7(bit_extender_1_out), .out({NZVC[3], out_5[6:0]}),
    .sel(Op_Code));  // open: en
  nor nor_2 (NZVC[2], out_5[0], out_5[1], out_5[2], out_5[3], out_5[4], out_5[5], out_5[6], NZVC[3]);
  // Probe on {NZVC[3], out_5[6:0]}

  assign out_5[7] = NZVC[3];

  // Notes on the sheet:
  //   ADD 000 et SUB 001
  //   NOT 010
  //   OR 011
  //   AND 100
  //   XOR 101
  //   SHIFT 110
  //   Not used anymore
endmodule

module AddSub (
  input  [7:0] A,
  input  [7:0] B,
  input  ADD_0_SUB_1,
  input  Is_Add_or_Sub,
  output [7:0] Result,
  output Carry
);

  wire adder_1_cout, xor_2_out;
  wire [7:0] bit_extender_1_out, xor_1_out;

  assign xor_1_out = B ^ bit_extender_1_out;  // XOR_Gate xor_1, 8 bits wide
  assign bit_extender_1_out = {{7{ADD_0_SUB_1}}, ADD_0_SUB_1};  // Bit_Extender bit_extender_1
  Adder adder_1 (.a(A), .b(xor_1_out), .out(Result), .cin(ADD_0_SUB_1), .cout(adder_1_cout));
  xor xor_2 (xor_2_out, adder_1_cout, ADD_0_SUB_1);
  and and_1 (Carry, xor_2_out, Is_Add_or_Sub);
endmodule

module Shift_unit (
  input  [7:0] A,
  input  [7:0] B,
  output [7:0] Shift_result
);

  wire [2:0] adder_1_out, not_1_out;
  wire [7:0] shifter_1_out, shifter_2_out;

  // Probe on B
  // Probe on B[2:0]
  assign not_1_out = ~B[2:0];  // NOT_Gate not_1, 3 bits wide
  Adder #(.width(3)) adder_1 (.a(not_1_out), .b(3'b001), .out(adder_1_out));  // open: cin, cout
  // Probe on adder_1_out
  Shifter shifter_1 (.in(A), .\dist (B[2:0]), .out(shifter_1_out));
  Shifter #(.shift("lr")) shifter_2 (.in(A), .\dist (adder_1_out), .out(shifter_2_out));
  Multiplexer #(.width(8), .disabled(0), .enable("false")) multiplexer_1 (
    .in0(shifter_1_out), .in1(shifter_2_out), .out(Shift_result), .sel(B[7]));

  // Notes on the sheet:
  //   Here, A is shifted by B, no overflow detection /!\
endmodule

module Overflow_detect (
  input  MSB_A,
  input  MSB_B,
  input  Is_Add_or_Sub,
  input  MSB_Result,
  input  _0_for_Add_1_for_Sub,
  output Overflow_FLAG
);

  wire and_1_out, and_2_out, multiplexer_1_out, xnor_1_out, xor_1_out, xor_2_out, xor_3_out;

  xnor xnor_1 (xnor_1_out, MSB_A, MSB_B);
  xor xor_1 (xor_1_out, MSB_A, MSB_Result);
  and and_1 (and_1_out, xnor_1_out, xor_1_out);
  xor xor_2 (xor_2_out, MSB_A, MSB_B);
  xor xor_3 (xor_3_out, MSB_A, MSB_Result);
  Multiplexer #(.disabled(0), .enable("false")) multiplexer_1 (
    .in0(and_1_out), .in1(and_2_out), .out(multiplexer_1_out), .sel(_0_for_Add_1_for_Sub));
  and and_2 (and_2_out, xor_2_out, xor_3_out);
  and and_3 (Overflow_FLAG, multiplexer_1_out, Is_Add_or_Sub);
endmodule

module Register_File (
  input  [2:0] Source,
  input  [2:0] Target,
  input  [7:0] Write_Back__RD,
  input  Clk,
  input  RegWrite,
  input  [2:0] Destination,
  output [7:0] Destination__Store_ONLY,
  output [7:0] Source_2,
  output [7:0] Target_2
);

  wire decoder_1_out0, decoder_1_out1, decoder_1_out2, decoder_1_out3, decoder_1_out4, decoder_1_out5,
       decoder_1_out6, decoder_1_out7;
  wire [7:0] R0_q, R1_q, R2_q, R3_q, R4_q, R5_q, R6_q, R7_q;

  Decoder #(.select(3), .disabled(0)) decoder_1 (
    .out0(decoder_1_out0), .out1(decoder_1_out1), .out2(decoder_1_out2), .out3(decoder_1_out3),
    .out4(decoder_1_out4), .out5(decoder_1_out5), .out6(decoder_1_out6), .out7(decoder_1_out7),
    .sel(Destination), .en(RegWrite));
  Register R0 (.D(Write_Back__RD), .en(decoder_1_out0), .Q(R0_q), .clk(Clk));  // open: clr
  Register R1 (.D(Write_Back__RD), .en(decoder_1_out1), .Q(R1_q), .clk(Clk));  // open: clr
  Register R3 (.D(Write_Back__RD), .en(decoder_1_out3), .Q(R3_q), .clk(Clk));  // open: clr
  Register R2 (.D(Write_Back__RD), .en(decoder_1_out2), .Q(R2_q), .clk(Clk));  // open: clr
  // Probe on R2_q
  Register R4 (.D(Write_Back__RD), .en(decoder_1_out4), .Q(R4_q), .clk(Clk));  // open: clr
  Register R5 (.D(Write_Back__RD), .en(decoder_1_out5), .Q(R5_q), .clk(Clk));  // open: clr
  Register R6 (.D(Write_Back__RD), .en(decoder_1_out6), .Q(R6_q), .clk(Clk));  // open: clr
  Register R7 (.D(Write_Back__RD), .en(decoder_1_out7), .Q(R7_q), .clk(Clk));  // open: clr
  Multiplexer #(.select(3), .width(8)) multiplexer_1 (
    .in0(R0_q), .in1(R1_q), .in2(R2_q), .in3(R3_q), .in4(R4_q), .in5(R5_q), .in6(R6_q), .in7(R7_q),
    .out(Destination__Store_ONLY), .sel(Destination));  // open: en
  Multiplexer #(.select(3), .width(8)) multiplexer_2 (
    .in0(R0_q), .in1(R1_q), .in2(R2_q), .in3(R3_q), .in4(R4_q), .in5(R5_q), .in6(R6_q), .in7(R7_q),
    .out(Source_2), .sel(Source));  // open: en
  Multiplexer #(.select(3), .width(8)) multiplexer_3 (
    .in0(R0_q), .in1(R1_q), .in2(R2_q), .in3(R3_q), .in4(R4_q), .in5(R5_q), .in6(R6_q), .in7(R7_q),
    .out(Target_2), .sel(Target));  // open: en
endmodule

module Tests_progressifs (
  input  GO
);

  wire clock_1_out, new_decoder_1_halt, newfsm_1_memenable, newfsm_1_memwrite, newfsm_1_pc_increment,
       newfsm_1_regwrite, not_1_out;
  wire [1:0] newfsm_1_pcsource, newfsm_1_wbsource;
  wire [2:0] new_decoder_1_rd, new_decoder_1_rs, new_decoder_1_rt, newfsm_1_aluop, newfsm_1_state_register;
  wire [3:0] alu_1_nzvc, new_decoder_1_opcode;
  wire [5:0] new_decoder_1_load_store_offset;
  wire [7:0] adder_1_out, adder_2_out, alu_1_out_5, bit_extender_1_out, controlled_buffer_1_out,
       multiplexer_1_out, multiplexer_2_out, multiplexer_3_out, new_decoder_1_immediate_address,
       new_decoder_1_immediate_number, PC_q, register_file_1_destination__store_only,
       register_file_1_source_2, register_file_1_target_2;
  wire [15:0] IR_q, rom_1_data;

  Clock clock_1 (.out(clock_1_out));
  Register PC (.D(multiplexer_1_out), .en(newfsm_1_pc_increment), .Q(PC_q), .clk(clock_1_out));  // open: clr
  Adder adder_1 (.a(8'h1), .b(PC_q), .out(adder_1_out));  // open: cin, cout
  Adder adder_2 (.a(PC_q), .b(bit_extender_1_out), .out(adder_2_out));  // open: cin, cout
  Multiplexer #(.select(2), .width(8), .disabled(0), .enable("false")) multiplexer_1 (
    .in0(adder_1_out), .in1(adder_2_out), .in2(new_decoder_1_immediate_address),
    .in3(register_file_1_source_2), .out(multiplexer_1_out), .sel(newfsm_1_pcsource));
  ROM #(.dataWidth(16)) rom_1 (.addr(PC_q), .data(rom_1_data));  // open: sel
  // Probe on newfsm_1_pcsource
  Register #(.width(16)) IR (.D(rom_1_data), .Q(IR_q), .clk(clock_1_out));  // open: en, clr
  // Probe on newfsm_1_state_register
  NewFSM newfsm_1 (
    .NZVC(alu_1_nzvc), .State_Register(newfsm_1_state_register), .CLK(clock_1_out), .ALUOp(newfsm_1_aluop),
    .MemWrite(newfsm_1_memwrite), .PCSource(newfsm_1_pcsource), .RegWrite(newfsm_1_regwrite),
    .WBsource(newfsm_1_wbsource), .GO(GO), .PC_increment(newfsm_1_pc_increment),
    .Instruction_OPcode(new_decoder_1_opcode), .Halt(new_decoder_1_halt), .MemEnable(newfsm_1_memenable));
  New_Decoder new_decoder_1 (
    .Instruction(IR_q), .OPCODE(new_decoder_1_opcode), .Immediate_Address(new_decoder_1_immediate_address),
    .Load_Store_offset(new_decoder_1_load_store_offset), .Rt(new_decoder_1_rt), .Rd(new_decoder_1_rd),
    .Rs(new_decoder_1_rs), .Immediate_Number(new_decoder_1_immediate_number), .Halt(new_decoder_1_halt));
  Multiplexer #(.select(2), .width(8), .disabled(0), .enable("false")) multiplexer_2 (
    .in0(new_decoder_1_immediate_number), .in1(adder_1_out), .in2(controlled_buffer_1_out),
    .in3(alu_1_out_5), .out(multiplexer_2_out), .sel(newfsm_1_wbsource));
  assign bit_extender_1_out = {{2{new_decoder_1_load_store_offset[5]}}, new_decoder_1_load_store_offset};  // Bit_Extender bit_extender_1
  assign controlled_buffer_1_out = newfsm_1_memwrite ? register_file_1_destination__store_only : 8'bz;  // Controlled_Buffer controlled_buffer_1
  Register_File register_file_1 (
    .Source(new_decoder_1_rs), .Target(new_decoder_1_rt), .Write_Back__RD(multiplexer_2_out),
    .Clk(clock_1_out), .Destination(new_decoder_1_rd), .Source_2(register_file_1_source_2),
    .Target_2(register_file_1_target_2), .Destination__Store_ONLY(register_file_1_destination__store_only),
    .RegWrite(newfsm_1_regwrite));
  Multiplexer #(.width(8), .disabled(0), .enable("false")) multiplexer_3 (
    .in0(register_file_1_target_2), .in1(bit_extender_1_out), .out(multiplexer_3_out),
    .sel(newfsm_1_memenable));
  // Probe on newfsm_1_wbsource
  ALU alu_1 (
    .A(register_file_1_source_2), .B(multiplexer_3_out), .Op_Code(newfsm_1_aluop), .NZVC(alu_1_nzvc),
    .out_5(alu_1_out_5));
  not not_1 (not_1_out, newfsm_1_memwrite);
  RAM ram_1 (
    .addr(alu_1_out_5), .data(controlled_buffer_1_out), .sel(newfsm_1_memenable), .clk(clock_1_out),
    .ld(not_1_out));  // open: clr
  // Probe on controlled_buffer_1_out

  // Notes on the sheet:
  //   PC+1
  //   Instruction memory
  //   contents of rom_1 (hex, n*v repeats v):
  //   2423 265e 4010 f000 12*0 96d0 1600 5000
endmodule

module NewFSM (
  input  [3:0] Instruction_OPcode,
  input  Halt,
  input  [3:0] NZVC,
  input  GO,
  input  CLK,
  output [2:0] ALUOp,
  output MemEnable,
  output [1:0] PCSource,
  output [1:0] WBsource,
  output MemWrite,
  output RegWrite,
  output [2:0] State_Register,
  output PC_increment
);

  wire and_1_out, and_2_out, and_3_out, and_4_out, and_5_out, and_6_out, and_7_out, and_8_out, and_9_out,
       and_10_out, and_11_out, and_12_out, decoder_1_out0, decoder_1_out1, decoder_1_out2, decoder_1_out3,
       decoder_1_out4, decoder_1_out5, decoder_1_out6, decoder_1_out7, decoder_2_out0, decoder_2_out1,
       decoder_2_out2, decoder_2_out3, decoder_2_out5, nor_1_out, nor_2_out, not_1_out, not_2_out, or_1_out,
       or_2_out, or_3_out, or_4_out, xor_1_out;
  wire [2:0] controlled_buffer_1_out, multiplexer_1_out;

  not not_1 (not_1_out, Instruction_OPcode[3]);
  Decoder #(.select(3), .disabled(0)) decoder_1 (
    .out0(decoder_1_out0), .out1(decoder_1_out1), .out2(decoder_1_out2), .out3(decoder_1_out3),
    .out4(decoder_1_out4), .out5(decoder_1_out5), .out6(decoder_1_out6), .out7(decoder_1_out7),
    .sel(Instruction_OPcode[2:0]), .en(not_1_out));
  and and_1 (and_1_out, decoder_1_out7, NZVC[2]);
  xor xor_1 (xor_1_out, NZVC[1], NZVC[3]);
  assign controlled_buffer_1_out = decoder_2_out0 ? 3'b001 : 3'bz;  // Controlled_Buffer controlled_buffer_1
  Multiplexer #(.width(3), .disabled(0), .enable("false")) multiplexer_1 (
    .in0(3'b000), .in1(3'b001), .out(multiplexer_1_out), .sel(Instruction_OPcode[2]));
  and and_2 (and_2_out, decoder_1_out6, xor_1_out);
  nor nor_1 (nor_1_out, decoder_1_out2, Halt);
  and and_3 (and_3_out, nor_1_out, decoder_2_out1);
  assign controlled_buffer_1_out = and_3_out ? 3'b010 : 3'bz;  // Controlled_Buffer controlled_buffer_2
  Multiplexer #(.width(3), .disabled(0), .enable("false")) multiplexer_2 (
    .in0(Instruction_OPcode[2:0]), .in1(multiplexer_1_out), .out(ALUOp), .sel(not_1_out));
  or or_1 (or_1_out, and_1_out, and_2_out);
  and and_4 (and_4_out, or_3_out, decoder_2_out2);
  and and_5 (and_5_out, or_4_out, decoder_2_out2);
  assign controlled_buffer_1_out = and_5_out ? 3'b011 : 3'bz;  // Controlled_Buffer controlled_buffer_3
  not not_2 (not_2_out, Halt);
  and and_6 (and_6_out, not_2_out, Instruction_OPcode[3]);
  and and_7 (and_7_out, decoder_1_out0, decoder_2_out3);
  and and_8 (and_8_out, decoder_2_out1, decoder_1_out2);
  or or_2 (or_2_out, and_4_out, and_7_out, and_8_out);
  assign controlled_buffer_1_out = or_2_out ? 3'b100 : 3'bz;  // Controlled_Buffer controlled_buffer_4
  or or_3 (or_3_out, and_6_out, decoder_1_out4);
  and and_9 (and_9_out, Halt, decoder_2_out1);
  assign controlled_buffer_1_out = and_9_out ? 3'b101 : 3'bz;  // Controlled_Buffer controlled_buffer_5
  or or_4 (or_4_out, decoder_1_out0, decoder_1_out1);
  nor nor_2 (nor_2_out, or_4_out, or_3_out);
  and and_10 (and_10_out, nor_2_out, decoder_2_out2);
  and and_11 (and_11_out, decoder_1_out1, decoder_2_out3);
  or or_5 (PC_increment, RegWrite, and_11_out, and_10_out, and_12_out);
  assign controlled_buffer_1_out = PC_increment ? 3'b000 : 3'bz;  // Controlled_Buffer controlled_buffer_6
  and and_12 (and_12_out, decoder_2_out5, GO);
  Register #(.width(3)) SRegister (.D(controlled_buffer_1_out), .Q(State_Register), .clk(CLK));  // open: en, clr
  and and_13 (MemWrite, decoder_1_out1, decoder_2_out3);
  Decoder #(.select(3), .disabled(0), .enable("false")) decoder_2 (
    .out0(decoder_2_out0), .out1(decoder_2_out1), .out2(decoder_2_out2), .out3(decoder_2_out3),
    .out4(RegWrite), .out5(decoder_2_out5), .sel(State_Register));  // open: out6, out7
  or or_6 (MemEnable, decoder_1_out0, decoder_1_out1);
  or or_7 (PCSource[1], decoder_1_out3, decoder_1_out4, decoder_1_out5);
  or or_8 (PCSource[0], decoder_1_out5, or_1_out);
  nor nor_3 (WBsource[1], decoder_1_out4, decoder_1_out2);
  nor nor_4 (WBsource[0], decoder_1_out2, decoder_1_out0);

  // Notes on the sheet:
  //   ADD
  //   SUB
  //   Fetch 0
  //   Decode 1
  //   Execute 2
  //   Memory 3
  //   Write back 4
  //   Stop 5
endmodule

module New_Decoder (
  input  [15:0] Instruction,
  output [7:0] Immediate_Address,
  output [7:0] Immediate_Number,
  output [3:0] OPCODE,
  output [5:0] Load_Store_offset,
  output [2:0] Rt,
  output [2:0] Rd,
  output Halt,
  output [2:0] Rs
);

  wire decoder_1_out4, decoder_1_out5, decoder_1_out6, decoder_1_out7, or_1_out;
  wire [2:0] multiplexer_2_out;

  Decoder #(.select(4)) decoder_1 (
    .out4(decoder_1_out4), .out5(decoder_1_out5), .out6(decoder_1_out6), .out7(decoder_1_out7), .out15(Halt),
    .sel(Instruction[15:12]));  // open: out0, out1, out2, out3, out8, out9, out10, out11, out12, out13, out14, en
  or or_1 (or_1_out, decoder_1_out6, decoder_1_out7);
  Multiplexer #(.width(3), .disabled(0), .enable("false")) multiplexer_1 (
    .in0(Instruction[5:3]), .in1(Instruction[8:6]), .out(Rt), .sel(or_1_out));
  Multiplexer #(.width(3), .disabled(0), .enable("false")) multiplexer_2 (
    .in0(Instruction[8:6]), .in1(Instruction[11:9]), .out(multiplexer_2_out), .sel(or_1_out));
  Multiplexer #(.width(3), .disabled(0), .enable("false")) multiplexer_3 (
    .in0(Instruction[11:9]), .in1(3'b111), .out(Rd), .sel(decoder_1_out4));
  Multiplexer #(.width(3), .disabled(0), .enable("false")) multiplexer_4 (
    .in0(multiplexer_2_out), .in1(3'b111), .out(Rs), .sel(decoder_1_out5));

  assign Immediate_Address = Instruction[7:0];
  assign Immediate_Number = Instruction[7:0];
  assign Load_Store_offset = Instruction[5:0];
  assign OPCODE = Instruction[15:12];

  // Notes on the sheet:
  //   R7 is the destination for CALL
  //   R7 is the source for RET
endmodule
